# Fritzing sketch sonoff-button (saved by Fritzing 0.9.4)

parts:
  Sonoff_Basic_R1 = Sonoff Basic R2 [package="DIP (Dual Inline) [THT]"]
  S3 = Round Pushbutton

nets:
  N1: Sonoff_Basic_R1.GND, S3.leg1
  N2: Sonoff_Basic_R1.LED, S3.leg0
