# Fritzing sketch sonoff-ftdi (saved by Fritzing 0.9.4)

parts:
  Sonoff_Basic_R1 = Sonoff Basic R2 [package="DIP (Dual Inline) [THT]"]
  Part2 = FTDI Basic Programmer

nets:
  N1: Sonoff_Basic_R1.3V3, Part2.POWER
  N2: Sonoff_Basic_R1.RX, Part2.TXO
  N3: Sonoff_Basic_R1.TX, Part2.RXI
  GND: Sonoff_Basic_R1.GND, Part2.GND
